# Fritzing sketch Mimic_Project (saved by Fritzing 0.9.3b)
breadboards: 1

parts:
  Part1 = Tri-Axis Gyro Breakout - L3G4200D
  R1 = Basic Flex Resistor
  Part2 = Arduino Ethernet Shield (Rev3)
  LED1 = RGB LED (com. cathode, rbg) [package="5 mm [THT]"]
  J6 = Piezo Speaker
  R2 = Resistor [tolerance=±5% resistance=220 package="0402 [SMD]"]
  J7 = Basic Servo
  J8 = Basic Servo
  J9 = Basic Servo
  J3 = Basic Servo
  R3 = Resistor [tolerance=±5% resistance=220 package=THT]

nets:
  GND: Part1.GND, R1.pin_1, Part2.GND, J6.pin1, J3.gnd
  VCC: Part1.VCC, Part2.3V3
  N1: Part1.SCL, Part2.A5/SCL
  N2: Part1.SDA, Part2.A4/SDA
  N3: Part1.INT1, Part2.D2
  N4: R1.Pin_2, Part2.A0, R2.Pin_1
  N5: Part2.PWM_D9, J3.pulse
  N6: Part2.ETH_CS, J7.pulse
  N7: Part2.PWM_D11, J8.pulse
  N8: Part2.SPI/D12, J9.pulse
  N9: Part2.SPI/D13, J6.pin2
  N10: Part2.PWM_D5, LED1.blue_anode
  N11: Part2.PWM_D6, LED1.green_anode
  N12: Part2.5V, R2.Pin_0
  N13: LED1.common_cathode, R3.Pin_0
